# Fritzing sketch keyboardMapper (saved by Fritzing 0.9.3b)
breadboards: 1

parts:
  Part1 = Arduino Mega 2560 (Rev3)
  IC2 = IC, DIP package, 28 pins [chip_label=MT8808ea]
  J1 = male pin header, 20 pins [form="♂ (male)"]
  R1 = Resistor [tolerance=±5% resistance=10k package=THT]
  Q1 = NPN-Transistor [part_number=BC547B package="TO92 [THT]"]

nets:
  N1: Part1.3V3, IC2.pin19
  N2: Part1.D31, IC2.pin24
  N3: Part1.D33, IC2.pin25
  N4: Part1.D35, IC2.pin26
  N5: Part1.D37, IC2.pin27
  N6: Part1.D39, IC2.pin28
  N7: Part1.D41, IC2.pin1
  N8: Part1.D43, IC2.pin4
  N9: Part1.D45, IC2.pin2
  N10: Part1.D47, IC2.pin10
  N11: Part1.D49, R1.Pin_0
  N12: Part1.GND, IC2.pin3, IC2.pin5
  N13: IC2.pin6, J1.pin13
  N14: IC2.pin7, J1.pin18
  N15: IC2.pin8, J1.pin16
  N16: IC2.pin9, J1.pin14
  N17: IC2.pin11, J1.pin9
  N18: IC2.pin12, J1.pin6
  N19: IC2.pin13, J1.pin7
  N20: IC2.pin14, J1.pin8
  N21: IC2.pin15, J1.pin5
  N22: IC2.pin16, J1.pin10
  N23: IC2.pin17, J1.pin11
  N24: IC2.pin18, J1.pin12
  N25: IC2.pin20, J1.pin20
  N26: IC2.pin21, J1.pin15
  N27: IC2.pin22, J1.pin17
  N28: IC2.pin23, J1.pin19
  N29: J1.pin1, Q1.E
  N30: J1.pin3, Q1.B
  N31: R1.Pin_1, Q1.C

notes:
  C64 Keyboard Port
  Via USB to computer
  1
  20
  no connection
  ground ->
  restore ->
  rows
  columns
  5V ->
